# Fritzing sketch 1 (saved by Fritzing 0.8.7b)
breadboards: 1

parts:
  LCD1 = LCD screen
  R1 = Rotary Potentiometer (Small) [maximum_resistance=100kΩ package=THT]
  Part1 = Arduino Uno (Rev3)
  LED1 = LED - 5mm [color="Red (633nm)" package="5 mm [THT]"]
  R2 = Resistor [tolerance=±5% resistance=220 package=THT]
  R3 = PHOTOCELL [package=photocell]

nets:
  VSS: LCD1.VSS, LCD1.R/W, R1.leg1, Part1.GND, LED1.cathode, R2.Pin_1
  VDD: LCD1.VDD, R1.leg2, Part1.5V, R3.P$1
  N1: LCD1.V0, R1.wiper
  N2: LCD1.RS, Part1.D12/MISO
  N3: LCD1.E, Part1.D11_PWM/MOSI
  N4: LCD1.DB4, Part1.D5_PWM
  N5: LCD1.DB5, Part1.D4
  N6: LCD1.DB6, Part1.D3_PWM
  N7: LCD1.DB7, Part1.D2
  N8: Part1.A0, R2.Pin_0, R3.P$2
  N9: Part1.D13/SCK, LED1.anode
