# Fritzing sketch 2 (saved by Fritzing 0.8.7b)
breadboards: 1

parts:
  U1 = HIH-4030 [package=hih-4030]
  Part1 = Arduino Uno (Rev3)
  R1 = Resistor [tolerance=±5% resistance=220 package=THT]
  R2 = Photocell (LDR) [package=THT]
  LED1 = LED - 5mm [color="Red (633nm)" package="5 mm [THT]"]  # not connected

nets:
  GND: U1.GND, Part1.GND, R1.Pin_1
  N1: U1.OUT, Part1.D2
  VCC: U1.VCC, Part1.5V
  N2: Part1.A0, R1.Pin_0, R2.pin_1
